# Fritzing sketch diagrama (saved by Fritzing 1.0.4)
breadboards: 1

parts:
  Esp8266 = Amica NodeMCU DEVKIT 1.0
  HC-SR04_Sensor = HC-SR04 Ultrasonic Distance Sensor
  Relay = 1 chan 5v relay module
  Buzzer = Passive Buzzer
  R1 = Resistor [tolerance=±5% power=0.25W resistance=1k package=THT]
  R2 = Resistor [tolerance=±5% power=0.25W resistance=15k package=THT]

nets:
  N1: Esp8266.pin1, Esp8266.pin_10, Esp8266.pin_26
  N2: Esp8266.pin2, Esp8266.pin_9, Esp8266.pin_18, Esp8266.pin_25, Esp8266.pin_29, HC-SR04_Sensor.GND, Relay.pin_1, Buzzer.NC, R2.Pin_1
  N3: Esp8266.pin5, Buzzer.S
  N4: Esp8266.pin6, R1.Pin_1, R2.Pin_0
  N5: Esp8266.pin8, Relay.pin_3
  N6: Esp8266.pin_14, HC-SR04_Sensor.TRIG
  N7: HC-SR04_Sensor.ECHO, R1.Pin_0
  N8: Relay.pin_2, Buzzer.-

custom parts:
  1 chan 5v relay module: 1 Channel 5V Relay Module Board Shield with Optocoupler Support High and Low Level Trigger for Arduino.
